# Fritzing sketch rgb (saved by Fritzing 0.9.3b)

parts:
  Raspberry_Pi_1 = Raspberry Pi 3 [part_number=RPI-3-V1.2]
  LED = RGB LED (com. cathode, rgb) [package="5 mm [THT]"]

nets:
  N1: Raspberry_Pi_1.GPIO18, LED.blue_anode
  N2: Raspberry_Pi_1.GPIO15, LED.green_anode
  N3: Raspberry_Pi_1.GPIO14, LED.red_anode
  N4: Raspberry_Pi_1.GND, LED.common_cathode
